# Fritzing sketch Environment (saved by Fritzing 0.9.3b)
breadboards: 1

parts:
  U1 = NodeMCU V1.0
  RHT1 = Humidity and Temperature Sensor RHT03
  HC-SR04_Sensor_1 = HC-SR04 Ultrasonic Distance Sensor

nets:
  N1: U1.D2, HC-SR04_Sensor_1.TRIG
  N2: U1.D3, HC-SR04_Sensor_1.ECHO
  N3: U1.D4, RHT1.Data-signal
  VCC: U1.3V3, RHT1.Vcc, HC-SR04_Sensor_1.VCC
  GND: U1.GND, RHT1.GND_1, HC-SR04_Sensor_1.GND

custom parts:
  NodeMCU V1.0: ESP8266 based NodeMCU
